# Fritzing sketch eyenizer_fritzing (saved by Fritzing 0.9.3b)
breadboards: 1

parts:
  Componente1 = Arduino Mega 2560 (Rev3)
  LCD1 = LCD screen
  J1 = Piezo Speaker
  R1 = Rotary Potentiometer (Small) [maximum_resistance=100kΩ package=THT]
  R2 = Resistor [tolerance=±5% resistance=220 package=THT]  # not connected
  R3 = Resistor [tolerance=±5% resistance=220 package=THT]
  LED1 = LED - 5mm [color="Red (633nm)" package="5 mm [THT]"]
  LED2 = LED - 5mm [color="Green (555nm)" package="5 mm [THT]"]
  ZS-042_RTC1 = ZS-042 RTC Module
  Componente2 = MicroSD Card Module
  Componente3 = RFID USB Reader

nets:
  N1: Componente1.D20/SDA, ZS-042_RTC1.SDA
  GND: Componente1.GND, LCD1.VSS, LCD1.LED-, J1.pin1, LED1.anode, LED2.anode, ZS-042_RTC1.GND, Componente2.GND, Componente3.TX-O
  3V3: Componente1.3V3, Componente3.VCC
  VCC: Componente1.5V, LCD1.VDD, LCD1.LED+, ZS-042_RTC1.VCC, Componente2.VCC
  N2: Componente1.D0_RX0, Componente2.CS
  N3: Componente1.D1_TX0, Componente3.GND
  N4: Componente1.D2_PWM, LCD1.DB4
  N5: Componente1.D3_PWM, LCD1.DB5
  N6: Componente1.D4_PWM, LCD1.DB6
  N7: Componente1.D5_PWM, LCD1.DB7
  N8: Componente1.D6_PWM, LCD1.RS
  N9: Componente1.D7_PWM, LCD1.E
  N10: Componente1.D50, Componente3.ANT1, Componente3.TX-O-RS232
  N11: Componente1.D51, Componente3.ANT2
  N12: Componente1.D52, Componente3.CP
  N13: Componente1.D53, Componente3.GNDT
  N14: LCD1.V0, R1.leg2
  N15: LCD1.R/W, R1.leg1
  N16: R3.Pin_0, LED1.cathode
